// Logisim project proje.circ as structural Verilog: 4 circuits, main circuit main
module main (
);

  wire ALU_zero, and_1_out, clk_out, controlunit_1_alusrc, controlunit_1_branch, controlunit_1_cond,
       controlunit_1_memread, controlunit_1_memtoreg, controlunit_1_memwrite, controlunit_1_regwrite,
       xor_1_out;
  wire [1:0] controlunit_1_aluop;
  wire [15:0] adder_1_out, adder_2_out, ALU_alu_result, bit_extender_1_out, multiplexer_1_out,
       multiplexer_2_out, multiplexer_3_out, PC_q, ram_1_data, REGFILE_readdata1, REGFILE_readdata2,
       rom_1_data, shifter_1_out;

  Register #(.width(16)) PC (.D(multiplexer_2_out), .en(1'b1), .Q(PC_q), .clk(clk_out));  // open: clr
  Adder #(.width(16)) adder_1 (.a(PC_q), .b(16'h1), .out(adder_1_out));  // open: cin, cout
  ROM #(.addrWidth(16), .dataWidth(16)) rom_1 (.addr(PC_q), .data(rom_1_data));  // open: sel
  Clock clk (.out(clk_out));
  assign bit_extender_1_out = {{11{rom_1_data[4]}}, rom_1_data[4:0]};  // Bit_Extender bit_extender_1
  RegisterFile REGFILE (
    .WriteData(multiplexer_3_out), .RegWrite(controlunit_1_regwrite), .WriteRegister(rom_1_data[10:8]),
    .clk(clk_out), .ReadRegister1(rom_1_data[7:5]), .ReadRegister2(rom_1_data[10:8]),
    .ReadData1(REGFILE_readdata1), .ReadData2(REGFILE_readdata2));
  Shifter #(.width(16), .shift("ar")) shifter_1 (.in(bit_extender_1_out), .\dist (4'b0001), .out(shifter_1_out));
  Multiplexer #(.width(16), .disabled(0), .enable("false")) multiplexer_1 (
    .in0(REGFILE_readdata2), .in1(bit_extender_1_out), .out(multiplexer_1_out), .sel(controlunit_1_alusrc));
  ControlUnit controlunit_1 (
    .Opcode(rom_1_data[15:11]), .RegWrite(controlunit_1_regwrite), .AluSrc(controlunit_1_alusrc),
    .MemRead(controlunit_1_memread), .MemToReg(controlunit_1_memtoreg), .Branch(controlunit_1_branch),
    .MemWrite(controlunit_1_memwrite), .Cond(controlunit_1_cond), .AluOp(controlunit_1_aluop));
  Adder #(.width(16)) adder_2 (.a(PC_q), .b(shifter_1_out), .out(adder_2_out));  // open: cin, cout
  ALU ALU (
    .A_in(REGFILE_readdata1), .B_in(multiplexer_1_out), .AluOP(controlunit_1_aluop),
    .Alu_result(ALU_alu_result), .Zero(ALU_zero));
  xor xor_1 (xor_1_out, controlunit_1_cond, ALU_zero);
  RAM #(.addrWidth(16), .dataWidth(16), .bus("separate")) ram_1 (
    .addr(ALU_alu_result), .din(REGFILE_readdata2), .data(ram_1_data), .str(controlunit_1_memwrite),
    .clk(clk_out), .ld(controlunit_1_memread));  // open: sel, clr
  and and_1 (and_1_out, xor_1_out, controlunit_1_branch);
  Multiplexer #(.width(16), .disabled(0), .enable("false")) multiplexer_2 (
    .in0(adder_1_out), .in1(adder_2_out), .out(multiplexer_2_out), .sel(and_1_out));
  Multiplexer #(.width(16), .disabled(0), .enable("false")) multiplexer_3 (
    .in0(ALU_alu_result), .in1(ram_1_data), .out(multiplexer_3_out), .sel(controlunit_1_memtoreg));

  // Notes on the sheet:
  //   contents of rom_1 (hex, n*v repeats v):
  //   100 200 304 2440 e85 3e04 121 241 3a76 2904 3000
  //   LSB
  //   MSB
  //   Opcode
  //   Zero : 1 XOR Cond : 0 == 1(BEQ)
endmodule

module RegisterFile (
  input  [2:0] ReadRegister1,
  input  RegWrite,
  input  [2:0] WriteRegister,
  input  [15:0] WriteData,
  input  clk,
  input  [2:0] ReadRegister2,
  output [15:0] ReadData1,
  output [15:0] ReadData2
);

  wire demultiplexer_1_out0, demultiplexer_1_out1, demultiplexer_1_out2, demultiplexer_1_out3,
       demultiplexer_1_out4, demultiplexer_1_out5, demultiplexer_1_out6, demultiplexer_1_out7;
  wire [15:0] X0_q, X1_q, X2_q, X3_q, X4_q, X5_q, X6_q, X7_q;

  Demultiplexer #(.select(3), .disabled(0), .enable("false")) demultiplexer_1 (
    .out0(demultiplexer_1_out0), .out1(demultiplexer_1_out1), .out2(demultiplexer_1_out2),
    .out3(demultiplexer_1_out3), .out4(demultiplexer_1_out4), .out5(demultiplexer_1_out5),
    .out6(demultiplexer_1_out6), .out7(demultiplexer_1_out7), .in(RegWrite), .sel(WriteRegister));
  Register #(.width(16)) X0 (.D(WriteData), .en(demultiplexer_1_out0), .Q(X0_q), .clk(clk));  // open: clr
  Register #(.width(16)) X1 (.D(WriteData), .en(demultiplexer_1_out1), .Q(X1_q), .clk(clk));  // open: clr
  Register #(.width(16)) X2 (.D(WriteData), .en(demultiplexer_1_out2), .Q(X2_q), .clk(clk));  // open: clr
  Register #(.width(16)) X3 (.D(WriteData), .en(demultiplexer_1_out3), .Q(X3_q), .clk(clk));  // open: clr
  Register #(.width(16)) X4 (.D(WriteData), .en(demultiplexer_1_out4), .Q(X4_q), .clk(clk));  // open: clr
  Register #(.width(16)) X5 (.D(WriteData), .en(demultiplexer_1_out5), .Q(X5_q), .clk(clk));  // open: clr
  Register #(.width(16)) X6 (.D(WriteData), .en(demultiplexer_1_out6), .Q(X6_q), .clk(clk));  // open: clr
  Register #(.width(16)) X7 (.D(WriteData), .en(demultiplexer_1_out7), .Q(X7_q), .clk(clk));  // open: clr
  Multiplexer #(.select(3), .width(16), .enable("false")) multiplexer_1 (
    .in0(X0_q), .in1(X1_q), .in2(X2_q), .in3(X3_q), .in4(X4_q), .in5(X5_q), .in6(X6_q), .in7(X7_q),
    .out(ReadData1), .sel(ReadRegister1));
  Multiplexer #(.select(3), .width(16), .enable("false")) multiplexer_2 (
    .in0(X0_q), .in1(X1_q), .in2(X2_q), .in3(X3_q), .in4(X4_q), .in5(X5_q), .in6(X6_q), .in7(X7_q),
    .out(ReadData2), .sel(ReadRegister2));
endmodule

module ALU (
  input  [15:0] A_in,
  input  [15:0] B_in,
  input  [1:0] AluOP,
  output [15:0] Alu_result,
  output Zero
);

  wire [15:0] adder_1_out, and_1_out, or_1_out, subtractor_1_out;

  Adder #(.width(16)) adder_1 (.a(A_in), .b(B_in), .out(adder_1_out));  // open: cin, cout
  Subtractor #(.width(16)) subtractor_1 (.a(A_in), .b(B_in), .out(subtractor_1_out));  // open: bin, bout
  assign and_1_out = A_in & B_in;  // AND_Gate and_1, 16 bits wide
  assign or_1_out = A_in | B_in;  // OR_Gate or_1, 16 bits wide
  Multiplexer #(.select(2), .width(16)) multiplexer_1 (
    .in0(adder_1_out), .in1(subtractor_1_out), .in2(and_1_out), .in3(or_1_out), .out(Alu_result), .sel(AluOP));  // open: en
  nor nor_1 (Zero, Alu_result[0], Alu_result[1], Alu_result[2], Alu_result[3], Alu_result[4], Alu_result[5], Alu_result[6], Alu_result[7], Alu_result[8], Alu_result[9], Alu_result[10], Alu_result[11], Alu_result[12], Alu_result[13], Alu_result[14], Alu_result[15]);
endmodule

module ControlUnit (
  input  [4:0] Opcode,
  output RegWrite,
  output AluSrc,
  output MemRead,
  output MemToReg,
  output Branch,
  output MemWrite,
  output Cond,
  output [1:0] AluOp
);

  wire ADDI_out, ANDI_out, ORI_out, SUBI_out;

  and ADDI (ADDI_out, ~Opcode[0], ~Opcode[1], ~Opcode[2], ~Opcode[3], ~Opcode[4]);  // AND_Gate
  and SUBI (SUBI_out, Opcode[0], ~Opcode[1], ~Opcode[2], ~Opcode[3], ~Opcode[4]);  // AND_Gate
  and ANDI (ANDI_out, ~Opcode[0], Opcode[1], ~Opcode[2], ~Opcode[3], ~Opcode[4]);  // AND_Gate
  and ORI (ORI_out, Opcode[0], Opcode[1], ~Opcode[2], ~Opcode[3], ~Opcode[4]);  // AND_Gate
  and LDR (MemRead, ~Opcode[0], ~Opcode[1], Opcode[2], ~Opcode[3], ~Opcode[4]);  // AND_Gate
  and STR (MemWrite, Opcode[0], ~Opcode[1], Opcode[2], ~Opcode[3], ~Opcode[4]);  // AND_Gate
  and u_Branch (Branch, Opcode[1], Opcode[2], ~Opcode[3], ~Opcode[4]);  // AND_Gate
  or or_1 (AluOp[0], SUBI_out, Branch, ORI_out);
  or or_2 (AluOp[1], ANDI_out, ORI_out);
  or or_3 (RegWrite, ADDI_out, SUBI_out, ANDI_out, ORI_out, MemRead);
  or or_4 (AluSrc, ADDI_out, SUBI_out, ANDI_out, ORI_out, MemRead, MemWrite);

  assign Cond = Opcode[0];
  assign MemToReg = MemRead;

  // Notes on the sheet:
  //   0 -> LSB
  //   negate 1 -> LSB
  //   00000 : ADDı
  //   00001 : SUBI
  //   00010 : ANDI
  //   00011 : ORI
  //   00100 : LDR
  //   00101 : STR
  //   00110 : BEQ
  //   00111 : BNE
  //   AluSrc = 0 Branch komutu
  //   AluSrc = 1 ADD komutu
endmodule
